# Fritzing sketch DIY-Auto (saved by Fritzing 0.9.6)
breadboards: 1

parts:
  C2 = Ceramic Capacitor [package="100 mil [THT, multilayer]"]
  C1 = Electrolytic Capacitor [capacitance=470µF voltage=16V package="200 mil [THT, electrolytic]"]
  C7 = Ceramic Capacitor [package="100 mil [THT, multilayer]"]
  R7 = Resistor [resistance=20000 package=THT]
  D1 = Schottky Diode [package="300 mil [THT]"]
  R6 = Resistor [resistance=1000 package=THT]
  ESP32 = ESP32 DevKit v1 (30 pins)
  Accu = Accu 7,4 V 1500 mAh (ERYNK)
  TB6612FNG = TB6612FNG-module
  M1 = DC Motor
  M2 = DC Motor
  LM2596 = LM2596
  SERVO = SERVO

nets:
  GND: C2.0, C1.-, C7.0, R7.Pin_0, ESP32.J2.14_GND, Accu.-, TB6612FNG.GND, LM2596.IN-, LM2596.OUT-, SERVO.GND
  N1: C2.1, C1.+, Accu.+, TB6612FNG.VM, LM2596.IN+
  N2: C7.1, D1.anode, LM2596.OUT+, SERVO.+5V
  N3: R7.Pin_1, ESP32.J3.7_D18, TB6612FNG.STBY
  N4: D1.cathode, ESP32.J2.15_VIN
  N5: R6.Pin_0, ESP32.J3.6_D19
  N6: R6.Pin_1, SERVO.SIG
  N7: ESP32.J2.6_D32, TB6612FNG.BIN1
  N8: ESP32.J2.7_D33, TB6612FNG.BIN2
  N9: ESP32.J2.8_D25, TB6612FNG.AIN1
  N10: ESP32.J2.9_D26, TB6612FNG.AIN2
  N11: ESP32.J2.10_D27, TB6612FNG.PWMA
  N12: ESP32.J3.11_D4, TB6612FNG.PWMB
  N13: ESP32.J3.15_3V3, TB6612FNG.VCC
  N14: TB6612FNG.B01, M2.pin_1
  N15: TB6612FNG.B02, M2.pin_2
  N16: TB6612FNG.A02, M1.pin_2
  N17: TB6612FNG.A01, M1.pin_1
