# Fritzing sketch DIY-Auto_hbrug (saved by Fritzing 0.9.6)
breadboards: 2

parts:
  C2 = Ceramic Capacitor [package="100 mil [THT, multilayer]"]
  C1 = Electrolytic Capacitor [capacitance=470µF voltage=16V package="200 mil [THT, electrolytic]"]
  C7 = Ceramic Capacitor [package="100 mil [THT, multilayer]"]
  Q101 = Basic FET P-Channel [package="TO220 [THT]"]
  R101 = Resistor [resistance=5100 package=THT]
  Q102 = NPN-Transistor [package="TO92 [THT]"]
  R102 = Resistor [resistance=5100 package=THT]
  R103 = Resistor [resistance=20000 package=THT]
  Q103 = Basic FET N-Channel [package="TO220 [THT]"]
  R104 = Resistor [resistance=1000 package=THT]
  R105 = Resistor [resistance=20000 package=THT]
  Q111 = Basic FET P-Channel [package="TO220 [THT]"]
  R111 = Resistor [resistance=5100 package=THT]
  Q112 = NPN-Transistor [package="TO92 [THT]"]
  R112 = Resistor [resistance=5100 package=THT]
  R113 = Resistor [resistance=20000 package=THT]
  Q113 = Basic FET N-Channel [package="TO220 [THT]"]
  R114 = Resistor [resistance=1000 package=THT]
  R115 = Resistor [resistance=20000 package=THT]
  R_T = Resistor [resistance=1000 package=THT]
  LED_R = Red LED - 5mm [package="5 mm [THT]"]
  LED_G = LED - 5mm [color="Green (570nm)" package="5 mm [THT]"]
  Q201 = Basic FET P-Channel [package="TO220 [THT]"]
  R201 = Resistor [resistance=5100 package=THT]
  Q202 = NPN-Transistor [package="TO92 [THT]"]
  R202 = Resistor [resistance=5100 package=THT]
  R203 = Resistor [resistance=20000 package=THT]
  Q203 = Basic FET N-Channel [package="TO220 [THT]"]
  R204 = Resistor [resistance=1000 package=THT]
  R205 = Resistor [resistance=20000 package=THT]
  Q211 = Basic FET P-Channel [package="TO220 [THT]"]
  R211 = Resistor [resistance=5100 package=THT]
  Q212 = NPN-Transistor [package="TO92 [THT]"]
  R212 = Resistor [resistance=5100 package=THT]
  R213 = Resistor [resistance=20000 package=THT]
  Q213 = Basic FET N-Channel [package="TO220 [THT]"]
  R214 = Resistor [resistance=1000 package=THT]
  R215 = Resistor [resistance=20000 package=THT]
  D1 = Schottky Diode [package="300 mil [THT]"]
  R6 = Resistor [resistance=1000 package=THT]
  ESP32 = ESP32 DevKit v1 (30 pins)
  Accu = Accu 7,4 V 1500 mAh (ERYNK)
  M1 = DC Motor
  M2 = DC Motor
  LM2596 = LM2596
  SERVO = SERVO

nets:
  N1: C2.0, C1.-, C7.0, Q102.E, R103.Pin_0, Q103.source, R105.Pin_1, Q112.E, R113.Pin_0, Q113.source, R115.Pin_1, Q202.E, R203.Pin_0, Q203.source, R205.Pin_1, Q212.E, R213.Pin_0, Q213.source, R215.Pin_1, ESP32.J2.14_GND, Accu.-, LM2596.IN-, LM2596.OUT-, SERVO.GND
  N2: C2.1, C1.+, Q101.source, R101.Pin_0, Q111.source, R111.Pin_0, Q201.source, R201.Pin_0, Q211.source, R211.Pin_0, Accu.+, LM2596.IN+
  N3: C7.1, D1.anode, LM2596.OUT+, SERVO.+5V
  N4: Q101.gate, R101.Pin_1, Q102.C
  N5: Q101.drain, Q103.drain, R_T.Pin_0, M1.pin_1
  N6: Q102.B, R102.Pin_0, R103.Pin_1
  N7: R102.Pin_1, ESP32.J2.8_D25
  N8: Q103.gate, R104.Pin_0
  N9: R104.Pin_1, R105.Pin_0, ESP32.J2.10_D27
  N10: Q111.gate, R111.Pin_1, Q112.C
  N11: Q111.drain, Q113.drain, LED_R.cathode, LED_G.anode, M1.pin_2
  N12: Q112.B, R112.Pin_0, R113.Pin_1
  N13: R112.Pin_1, ESP32.J2.9_D26
  N14: Q113.gate, R114.Pin_0
  N15: R114.Pin_1, R115.Pin_0, ESP32.J2.13_D13
  N16: R_T.Pin_1, LED_R.anode, LED_G.cathode
  N17: Q201.gate, R201.Pin_1, Q202.C
  N18: Q201.drain, Q203.drain, M2.pin_1
  N19: Q202.B, R202.Pin_0, R203.Pin_1
  N20: R202.Pin_1, ESP32.J2.6_D32
  N21: Q203.gate, R204.Pin_0
  N22: R204.Pin_1, R205.Pin_0, ESP32.J3.11_D4
  N23: Q211.gate, R211.Pin_1, Q212.C
  N24: Q211.drain, Q213.drain, M2.pin_2
  N25: Q212.B, R212.Pin_0, R213.Pin_1
  N26: R212.Pin_1, ESP32.J2.7_D33
  N27: Q213.gate, R214.Pin_0
  N28: R214.Pin_1, R215.Pin_0, ESP32.J3.7_D18
  N29: D1.cathode, ESP32.J2.15_VIN
  N30: R6.Pin_0, ESP32.J3.6_D19
  N31: R6.Pin_1, SERVO.SIG
